// Logisim project rudimentary computing device.circ as structural Verilog: 1 circuit, main circuit main
module main (
  input  [5:0] in_1,
  input  [5:0] in_2,
  input  [5:0] in_3,
  input  in_4,
  input  in_5,
  input  in_6,
  input  in_7,
  input  in_8,
  input  in_9,
  output [5:0] out_10,
  output [5:0] out_11,
  output [5:0] out_12
);

  wire button_1_out, clock_1_out, main_2_a_b, main_2_a_b_2, main_2_add, main_2_insert, main_2_invert,
       main_2_out;
  wire [0:0] main_3_equality_check, main_4_out_13;
  wire [5:0] main_1_out_14, main_5_out_12, main_7_out_19, main_8_out_18, main_9_out_18, main_10_out_18,
       main_11_out_8, main_11_out_9, main_11_out_10, main_12_out_8, main_12_out_9, main_12_out_10,
       main_13_out_8, main_13_out_9, main_13_out_10, main_14_out_8, main_14_out_9, main_14_out_10,
       main_15_out_8, main_15_out_9, main_15_out_10;
  wire [18:0] rom_1_data;

  Clock clock_1 (.out(clock_1_out));
  LED led_1 (.in(main_1_out_14[4]));
  LED led_2 (.in(main_1_out_14[5]));
  Button button_1 (.out(button_1_out));
  LED led_3 (.in(main_1_out_14[3]));
  LED led_4 (.in(main_1_out_14[2]));
  LED led_5 (.in(main_1_out_14[0]));
  LED led_6 (.in(main_1_out_14[1]));
  program_counter_main main_1 (
    .in_7(button_1_out), .in_8(clock_1_out), .out_9(main_1_out_14[5]), .out_10(main_1_out_14[4]),
    .out_11(main_1_out_14[3]), .out_12(main_1_out_14[2]), .out_13(main_1_out_14[1]),
    .out_14(main_1_out_14[0]), .in_1(in_4), .in_2(in_5), .in_3(in_6), .in_4(in_7), .in_5(in_8), .in_6(in_9));
  instructor_main main_2 (
    .in_1(rom_1_data[18]), .in_2(rom_1_data[17]), .in_3(rom_1_data[16]), .in_4(rom_1_data[15]),
    .ADD(main_2_add), .INVERT(main_2_invert), .A_B(main_2_a_b), .A_B_2(main_2_a_b_2), .INSERT(main_2_insert),
    .OUT(main_2_out));  // open: A_B_3, STEP, HALT, out_14, out_15, out_16
  equality_check_main main_3 (
    .Equality_Check(main_3_equality_check[0]), .in_1(main_8_out_18[5]), .in_2(main_8_out_18[4]),
    .Number_A(main_8_out_18[3]), .in_4(main_8_out_18[2]), .in_5(main_8_out_18[1]), .in_6(main_8_out_18[0]),
    .in_7(main_9_out_18[5]), .in_8(main_9_out_18[4]), .in_9(main_9_out_18[3]), .in_10(main_9_out_18[2]),
    .in_11(main_9_out_18[1]), .in_12(main_9_out_18[0]));
  a_less_than_b_main main_4 (
    .in_7(main_9_out_18[5]), .in_8(main_9_out_18[4]), .in_9(main_9_out_18[3]), .in_10(main_9_out_18[2]),
    .in_11(main_9_out_18[1]), .in_12(main_9_out_18[0]), .in_1(main_8_out_18[5]), .in_2(main_8_out_18[4]),
    .in_3(main_8_out_18[3]), .in_4(main_8_out_18[2]), .in_5(main_8_out_18[1]), .in_6(main_8_out_18[0]),
    .out_13(main_4_out_13[0]));
  inverter_main main_5 (
    .in_1(main_8_out_18[5]), .in_2(main_8_out_18[4]), .in_3(main_8_out_18[3]), .in_4(main_8_out_18[2]),
    .in_5(main_8_out_18[1]), .in_6(main_8_out_18[0]), .out_7(main_5_out_12[5]), .out_8(main_5_out_12[4]),
    .out_9(main_5_out_12[3]), .out_10(main_5_out_12[2]), .out_11(main_5_out_12[1]), .out_12(main_5_out_12[0]));
  input_selector_main main_6 (
    .in_4(main_2_out), .in_1({6{1'b0}}), .in_2({6{1'b0}}), .in_3({6{1'b0}}), .in_5(main_8_out_18),
    .in_6(main_9_out_18), .in_7(main_10_out_18), .out_8(out_10), .out_9(out_11), .out_10(out_12));
  addition_main main_7 (
    .in_1(main_9_out_18[5]), .in_2(main_9_out_18[4]), .in_3(main_9_out_18[3]), .in_4(main_9_out_18[2]),
    .in_5(main_9_out_18[1]), .in_6(main_9_out_18[0]), .in_7(main_8_out_18[5]), .in_8(main_8_out_18[4]),
    .in_9(main_8_out_18[3]), .in_10(main_8_out_18[2]), .in_11(main_8_out_18[1]), .in_12(main_8_out_18[0]),
    .out_14(main_7_out_19[5]), .out_15(main_7_out_19[4]), .out_16(main_7_out_19[3]),
    .out_17(main_7_out_19[2]), .out_18(main_7_out_19[1]), .out_19(main_7_out_19[0]));  // open: out_13
  ROM #(.addrWidth(6), .dataWidth(19)) rom_1 (.addr(main_1_out_14), .data(rom_1_data));  // open: sel
  memory_main main_8 (
    .Address(rom_1_data[14]), .in_2(rom_1_data[13]), .Write(rom_1_data[12]), .in_4(rom_1_data[11]),
    .Read(rom_1_data[10]), .Initialise(button_1_out), .in_7(main_15_out_8[5]), .in_8(main_15_out_8[4]),
    .Input(main_15_out_8[3]), .in_10(main_15_out_8[2]), .in_11(main_15_out_8[1]), .in_12(main_15_out_8[0]),
    .out_13(main_8_out_18[5]), .out_14(main_8_out_18[4]), .Output(main_8_out_18[3]),
    .out_16(main_8_out_18[2]), .out_17(main_8_out_18[1]), .out_18(main_8_out_18[0]));
  memory_main main_9 (
    .Address(rom_1_data[9]), .in_2(rom_1_data[8]), .Write(rom_1_data[7]), .in_4(rom_1_data[6]),
    .Read(rom_1_data[5]), .Initialise(button_1_out), .in_7(main_15_out_9[5]), .in_8(main_15_out_9[4]),
    .Input(main_15_out_9[3]), .in_10(main_15_out_9[2]), .in_11(main_15_out_9[1]), .in_12(main_15_out_9[0]),
    .out_13(main_9_out_18[5]), .out_14(main_9_out_18[4]), .Output(main_9_out_18[3]),
    .out_16(main_9_out_18[2]), .out_17(main_9_out_18[1]), .out_18(main_9_out_18[0]));
  memory_main main_10 (
    .Address(rom_1_data[4]), .in_2(rom_1_data[3]), .Write(rom_1_data[2]), .in_4(rom_1_data[1]),
    .Read(rom_1_data[0]), .Initialise(button_1_out), .in_7(main_15_out_10[5]), .in_8(main_15_out_10[4]),
    .Input(main_15_out_10[3]), .in_10(main_15_out_10[2]), .in_11(main_15_out_10[1]),
    .in_12(main_15_out_10[0]), .out_13(main_10_out_18[5]), .out_14(main_10_out_18[4]),
    .Output(main_10_out_18[3]), .out_16(main_10_out_18[2]), .out_17(main_10_out_18[1]),
    .out_18(main_10_out_18[0]));
  input_selector_main main_11 (
    .in_4(main_2_a_b_2), .in_1({6{1'b0}}), .in_2({6{1'b0}}), .in_3({6{1'b0}}), .in_5({6{1'b0}}),
    .in_6({6{1'b0}}), .in_7({{5{1'b0}}, main_3_equality_check[0]}), .out_8(main_11_out_8),
    .out_9(main_11_out_9), .out_10(main_11_out_10));
  input_selector_main main_12 (
    .in_4(main_2_a_b), .in_1(main_11_out_8), .in_2(main_11_out_9), .in_3(main_11_out_10), .in_5({6{1'b0}}),
    .in_6({6{1'b0}}), .in_7({{5{1'b0}}, main_4_out_13[0]}), .out_8(main_12_out_8), .out_9(main_12_out_9),
    .out_10(main_12_out_10));
  input_selector_main main_13 (
    .in_4(main_2_invert), .in_1(main_12_out_8), .in_2(main_12_out_9), .in_3(main_12_out_10),
    .in_5({6{1'b0}}), .in_6({6{1'b0}}), .in_7(main_5_out_12), .out_8(main_13_out_8), .out_9(main_13_out_9),
    .out_10(main_13_out_10));
  input_selector_main main_14 (
    .in_4(main_2_insert), .in_1(main_13_out_8), .in_2(main_13_out_9), .in_3(main_13_out_10), .in_5(in_1),
    .in_6(in_2), .in_7(in_3), .out_8(main_14_out_8), .out_9(main_14_out_9), .out_10(main_14_out_10));
  input_selector_main main_15 (
    .in_4(main_2_add), .in_1(main_14_out_8), .in_2(main_14_out_9), .in_3(main_14_out_10), .in_5({6{1'b0}}),
    .in_6({6{1'b0}}), .in_7(main_7_out_19), .out_8(main_15_out_8), .out_9(main_15_out_9),
    .out_10(main_15_out_10));

  // Notes on the sheet:
  //   contents of rom_1 (hex, n*v repeats v):
  //   39800 380c0 94a6 40005 40000 39800 1140a 40009 9 a b c d e f
endmodule
